# Fritzing sketch maquina_espendedora (saved by Fritzing 0.9.6b)
breadboards: 1

parts:
  Part1 = Arduino Uno (Rev3)
  LED1 = LED - 5mm [color="Red (633nm)" current=0.030 package="5 mm [THT]"]
  LED2 = LED - 5mm [color="Green (565nm)" current=0.030 package="5 mm [THT]"]
  Part2 = Thumb Joystick
  U1 = LCD-16X2 [package=lcd-16x2]
  S1 = Momentary Switch [package=ksa_sealed_tac_switch]
  HC-SR04_Sensor_1 = HC-SR04 Ultrasonic Distance Sensor
  Mod1 = KY-015 Temperature & Humidity Sensor Module [package="Breakout board"]
  R1 = Resistor [tolerance=±5% power=0.25 resistance=220 package=THT]
  R2 = Resistor [tolerance=±5% power=0.25 resistance=220 package=THT]
  R3 = Resistor [tolerance=±5% power=0.25 resistance=220 package=THT]

nets:
  N1: Part1.A1, LED2.anode
  N2: Part1.A2, Part2.VERT
  N3: Part1.A3, Part2.HORZ
  N4: Part1.D8, HC-SR04_Sensor_1.TRIG
  N5: Part1.D9_PWM, Mod1.S
  N6: Part1.D10_PWM/SS, S1.3
  N7: Part1.D11_PWM/MOSI, U1.E
  N8: Part1.D12/MISO, U1.RS
  N9: Part1.D13/SCK, Part2.SEL
  N10: Part1.D2, U1.DB7
  N11: Part1.D3_PWM, U1.DB6
  N12: Part1.D4, U1.DB5
  N13: Part1.D5_PWM, U1.DB4
  N14: Part1.D6_PWM, LED1.anode
  N15: Part1.D7, HC-SR04_Sensor_1.ECHO
  VCC: Part1.5V, Part2.VCC, U1.VDD, HC-SR04_Sensor_1.VCC, Mod1.Vin, R3.Pin_1
  GND: Part1.GND, Part2.GND, U1.VSS, U1.VO, U1.R_W, U1.K, S1.1, HC-SR04_Sensor_1.GND, Mod1.-, R1.Pin_0, R2.Pin_0
  N16: LED1.cathode, R1.Pin_1
  N17: LED2.cathode, R2.Pin_1
  N18: U1.A, R3.Pin_0

custom parts:
  KY-015 Temperature & Humidity Sensor Module: KY-015 temperature and humidity sensor module, provides a low-latency serial interface to measure humidity and temperature.
